# Fritzing sketch RePETeR (saved by Fritzing 0.9.5d)
breadboards: 1

parts:
  RE1 = Rotary Encoder [package=THT]
  S1 = Pushbutton [package="[THT]"]
  Componente1 = Arduino Uno (Rev3)
  U1 = LCD-16X2 [package=lcd-16x2_noholes]
  Q1 = Basic FET N-Channel [package="D2Pak [SMD]"]
  U3 = L298_BRIDGE_DRIVER [package=powerso20]
  M1 = DC Motor
  L1 = Inductor [package="400 mil [THT]"]
  R3 = Temperature Sensor (Thermistor) [thermistor_type=NTC package=THT]
  R4 = Resistor [tolerance=±5% resistance=220 package=THT]

nets:
  N1: RE1.EncoderPinA, Componente1.D2
  GND: RE1.EncoderPinC, S1.Pin_3, S1.Pin_4, Componente1.GND, U3.GND, R3.pin_0
  N2: RE1.EncoderPinB, Componente1.D3_PWM
  N3: S1.Pin_1, S1.Pin_2, Componente1.D4
  N4: Componente1.A0, R4.Pin_1
  N5: Componente1.D8, U3.IN3
  N6: Componente1.A4/SDA, U1.VO
  N7: Componente1.A5/SCL, U1.RS
  N8: Componente1.D5_PWM, U3.ENB
  N9: Componente1.D6_PWM, Q1.Gate
  N10: Componente1.D7, U3.IN4
  5V: Componente1.5V, U1.VSS, R4.Pin_0
  N11: Q1.drain, L1.pin_0
  N12: U3.OUT3, M1.pin_1
  N13: U3.OUT4, M1.pin_2

notes:
  LCD i2c
  (SDA, SCL)
  Encoder con botón
  Divisor + termistor
  +5V arduino (VIN)
  Fuente 12V
  - +
  Calentador 24V
  + -
  Fuente 24V
